# Fritzing sketch Final_Fritzing_Breadboard (saved by Fritzing 0.9.3b)
breadboards: 2

parts:
  Raspberry_Pi_1 = Raspberry Pi 3 [part_number=RPI-3-V1.2]
  LCD1 = LCD screen
  R1 = Rotary Potentiometer (Small) [maximum_resistance=100kΩ package=THT]
  R2 = Resistor [tolerance=±5% resistance=10k package=THT]
  R3 = Resistor [tolerance=±5% resistance=330 package=THT]
  R4 = Resistor [tolerance=±5% resistance=10k package=THT]
  Matrix_keypad1 = KEYPAD 4x4
  R5 = Resistor [tolerance=±5% resistance=1k package=THT]
  R6 = Resistor [tolerance=±5% resistance=1k package=THT]
  R7 = Resistor [tolerance=±5% resistance=1k package=THT]
  R8 = Resistor [tolerance=±5% resistance=1k package=THT]
  Onderdeel1 = RFID-RC522-v2
  J1 = Power Jack [package=power_jack_pth_lock]
  LPD8806_RGB_LED_Strip1 = LPD8806 RGB LED Strip
  R9 = Photocell (LDR) [package=THT]
  R10 = Photocell (LDR) [package=THT]
  R11 = Photocell (LDR) [package=THT]
  R12 = Photocell (LDR) [package=THT]
  R13 = Photocell (LDR) [package=THT]
  R14 = Photocell (LDR) [package=THT]
  R15 = Resistor [tolerance=±5% resistance=10k package=THT]
  R16 = Resistor [tolerance=±5% resistance=10k package=THT]
  R17 = Resistor [tolerance=±5% resistance=10k package=THT]
  R18 = Resistor [tolerance=±5% resistance=10k package=THT]
  R19 = Resistor [tolerance=±5% resistance=10k package=THT]
  R20 = Resistor [tolerance=±5% resistance=10k package=THT]
  Q5 = TIP120 Hi-Current Darlington Transistor
  Q6 = TIP120 Hi-Current Darlington Transistor
  Q7 = TIP120 Hi-Current Darlington Transistor
  Q8 = TIP120 Hi-Current Darlington Transistor
  Q9 = TIP120 Hi-Current Darlington Transistor
  R22 = Resistor [tolerance=±5% resistance=220 package=THT]
  R23 = Resistor [tolerance=±5% resistance=220 package=THT]
  R27 = Resistor [tolerance=±5% resistance=220 package=THT]
  R28 = Resistor [tolerance=±5% resistance=220 package=THT]
  R29 = Resistor [tolerance=±5% resistance=10k package=THT]
  R30 = Resistor [tolerance=±5% resistance=10k package=THT]
  IC1 = MCP3008 8-channel 10-bit ADC [part_number=MCP3008]
  U1 = PCF8574 [package="DIP16 [THT]"]
  R21 = Resistor [tolerance=±5% resistance=220 package=THT]

nets (from the breadboard view):
  3V3: Raspberry_Pi_1.3v3, Raspberry_Pi_1.3V3, R2.Pin_1, R4.Pin_1, Onderdeel1.3.3V, R15.Pin_0, R16.Pin_0, R17.Pin_0, R18.Pin_0, R19.Pin_0, R20.Pin_0, R29.Pin_0, R30.Pin_0, IC1.no_name_yet#15, IC1.no_name_yet#16
  N1: Raspberry_Pi_1.GPIO2, R3.Pin_1, R4.Pin_0
  N2: Raspberry_Pi_1.GPIO3, U1.SCL
  N3: Raspberry_Pi_1.GPIO4, R28.Pin_0
  GND: Raspberry_Pi_1.GND, LCD1.VSS, LCD1.R/W, LCD1.LED-, R1.leg1, R1.leg2, Onderdeel1.GND, J1.GND, R9.pin_1, R10.pin_1, R11.pin_1, R12.pin_1, R13.pin_1, R14.pin_1, Q5.EMITTER, Q6.EMITTER, Q7.EMITTER, Q8.EMITTER, Q9.EMITTER, IC1.no_name_yet#9, IC1.no_name_yet#14, U1.A1
  N4: Raspberry_Pi_1.GPIO17, R5.Pin_0
  N5: Raspberry_Pi_1.GPIO27, R6.Pin_0
  N6: Raspberry_Pi_1.GPIO22, R7.Pin_1
  N7: Raspberry_Pi_1.GPIO10, Onderdeel1.MOSI, IC1.no_name_yet#11
  N8: Raspberry_Pi_1.GPIO9, Onderdeel1.MISO, IC1.no_name_yet#12
  N9: Raspberry_Pi_1.GPIO11, Onderdeel1.SCK, IC1.no_name_yet#13
  N10: Raspberry_Pi_1.GPIO5, R8.Pin_1
  N11: Raspberry_Pi_1.GPIO6, Matrix_keypad1.row1
  N12: Raspberry_Pi_1.GPIO13, Matrix_keypad1.row2
  N13: Raspberry_Pi_1.GPIO19, Matrix_keypad1.row3
  N14: Raspberry_Pi_1.GPIO26, Matrix_keypad1.row4
  N15: Raspberry_Pi_1.GPIO21, R21.Pin_0
  N16: Raspberry_Pi_1.GPIO20, R23.Pin_0
  N17: Raspberry_Pi_1.GPIO16, R22.Pin_0
  N18: Raspberry_Pi_1.GPIO12, R27.Pin_0
  N19: Raspberry_Pi_1.GPIO7, IC1.no_name_yet#10
  N20: Raspberry_Pi_1.GPIO8, Onderdeel1.SDA
  N21: Raspberry_Pi_1.GPIO25, Onderdeel1.RST
  N22: Raspberry_Pi_1.GPIO24, LCD1.E
  N23: Raspberry_Pi_1.GPIO23, LCD1.RS
  5V: Raspberry_Pi_1.5V, LCD1.VDD, LCD1.LED+
  N24: LCD1.V0, R1.wiper
  N25: LCD1.DB1, U1.P1
  N26: LCD1.DB5, U1.P5
  N27: LCD1.DB6, U1.P6
  N28: LCD1.DB7, U1.P7
  N29: R3.Pin_0, U1.SDA
  N30: Matrix_keypad1.col1, R5.Pin_1
  N31: Matrix_keypad1.col2, R6.Pin_1
  N32: Matrix_keypad1.col3, R7.Pin_0
  N33: Matrix_keypad1.col4, R8.Pin_0
  N34: J1.PWR, LPD8806_RGB_LED_Strip1.GND
  N35: LPD8806_RGB_LED_Strip1.DI, Q9.COLLECTOR
  N36: LPD8806_RGB_LED_Strip1.CI, Q8.COLLECTOR
  N37: LPD8806_RGB_LED_Strip1.+5V, Q7.COLLECTOR
  N38: R9.pin_0, R15.Pin_1, IC1.no_name_yet#8
  N39: R10.pin_0, R16.Pin_1, IC1.no_name_yet#7
  N40: R11.pin_0, R20.Pin_1, IC1.no_name_yet#3
  N41: R12.pin_0, R17.Pin_1
  N42: R13.pin_0, R18.Pin_1, IC1.no_name_yet#5
  N43: R14.pin_0, R19.Pin_1, IC1.no_name_yet#4
  N44: Q5.BASE, R27.Pin_1
  N45: Q6.BASE, R28.Pin_1
  N46: Q7.BASE, R21.Pin_1
  N47: Q8.BASE, R22.Pin_1
  N48: Q9.BASE, R23.Pin_1
  N49: R29.Pin_1, IC1.no_name_yet#1
  N50: R30.Pin_1, IC1.no_name_yet#2

notes:
  +12V
  B
  R
  G
  12v GND
  Slot 1
  12v GND
  Slot 2
  3.3v GND
  Magneet
  sensor2
  Magneetsensor1
  3.3v GND

custom parts:
  KEYPAD 4x4: Matrix keypad 16 buttons, 4 rows x 4 columns
  RFID-RC522-v2: A simple China made RFID-RC522 Reader; do check the pin labels, as this is a MFRC522 based clone.
  LPD8806 RGB LED Strip: Digitally addressable RGB LED strip
  PCF8574: 8-bit parallel-load shift registers
