# Fritzing sketch FritzingSchemaBreadboardV4 (saved by Fritzing 0.9.3b)
breadboards: 2

parts:
  Raspberry_Pi_1 = Raspberry Pi 3 [part_number=RPI-3-V1.2]
  LCD1 = LCD screen
  R1 = Rotary Potentiometer (Small) [maximum_resistance=100kΩ package=THT]
  R2 = Resistor [tolerance=±5% resistance=10k package=THT]
  R3 = Resistor [tolerance=±5% resistance=330 package=THT]
  R4 = Resistor [tolerance=±5% resistance=10k package=THT]
  Matrix_keypad1 = KEYPAD 4x4
  R5 = Resistor [tolerance=±5% resistance=1k package=THT]
  R6 = Resistor [tolerance=±5% resistance=1k package=THT]
  R7 = Resistor [tolerance=±5% resistance=1k package=THT]
  R8 = Resistor [tolerance=±5% resistance=1k package=THT]
  Onderdeel1 = RFID-RC522-v2
  J1 = Power Jack [package=power_jack_pth_lock]
  LPD8806_RGB_LED_Strip1 = LPD8806 RGB LED Strip
  ADC1 = MCP3008 [package=dil16]
  R9 = Photocell (LDR) [package=THT]
  R10 = Photocell (LDR) [package=THT]
  R11 = Photocell (LDR) [package=THT]
  R12 = Photocell (LDR) [package=THT]
  R13 = Photocell (LDR) [package=THT]
  R14 = Photocell (LDR) [package=THT]
  R15 = Resistor [tolerance=±5% resistance=10k package=THT]
  R16 = Resistor [tolerance=±5% resistance=10k package=THT]
  R17 = Resistor [tolerance=±5% resistance=10k package=THT]
  R18 = Resistor [tolerance=±5% resistance=10k package=THT]
  R19 = Resistor [tolerance=±5% resistance=10k package=THT]
  R20 = Resistor [tolerance=±5% resistance=10k package=THT]
  Q5 = TIP120 Hi-Current Darlington Transistor
  Q6 = TIP120 Hi-Current Darlington Transistor
  U2 = PCF8574 [package="DIP16 [THT]"]
  Q7 = TIP120 Hi-Current Darlington Transistor
  Q8 = TIP120 Hi-Current Darlington Transistor
  Q9 = TIP120 Hi-Current Darlington Transistor
  U3 = PCF8574 [package="DIP16 [THT]"]
  Q10 = TIP120 Hi-Current Darlington Transistor
  Q11 = TIP120 Hi-Current Darlington Transistor
  Q12 = TIP120 Hi-Current Darlington Transistor
  LPD8806_RGB_LED_Strip2 = LPD8806 RGB LED Strip
  R21 = Resistor [tolerance=±5% resistance=220 package=THT]
  R22 = Resistor [tolerance=±5% resistance=220 package=THT]
  R23 = Resistor [tolerance=±5% resistance=220 package=THT]
  R24 = Resistor [tolerance=±5% resistance=220 package=THT]
  R25 = Resistor [tolerance=±5% resistance=220 package=THT]
  R26 = Resistor [tolerance=±5% resistance=220 package=THT]
  R27 = Resistor [tolerance=±5% resistance=220 package=THT]
  R28 = Resistor [tolerance=±5% resistance=220 package=THT]
  R29 = Resistor [tolerance=±5% resistance=10k package=THT]
  R30 = Resistor [tolerance=±5% resistance=10k package=THT]

nets (from the breadboard view):
  VCC: Raspberry_Pi_1.3v3, R2.Pin_1, R4.Pin_1, Onderdeel1.3.3V, ADC1.VREF, ADC1.VDD, R15.Pin_0, R16.Pin_0, R17.Pin_0, R18.Pin_0, R19.Pin_0, R20.Pin_0, U2.VCC, U3.A0, U3.VCC, R29.Pin_0, R30.Pin_0
  N1: Raspberry_Pi_1.GPIO2, R3.Pin_1, R4.Pin_0
  N2: Raspberry_Pi_1.GPIO3, U2.SCL, U3.SDA
  N3: Raspberry_Pi_1.GPIO4, R28.Pin_0
  GND: Raspberry_Pi_1.GND, LCD1.VSS, LCD1.R/W, LCD1.LED-, R1.leg1, R1.leg2, Onderdeel1.GND, J1.GND, ADC1.DGND, ADC1.AGND, R9.pin_1, R10.pin_1, R11.pin_1, R12.pin_1, R13.pin_1, R14.pin_1, Q5.EMITTER, Q6.EMITTER, U2.A0, U2.A1, U2.A2, U2.GND, Q7.EMITTER, Q8.EMITTER, Q9.EMITTER, U3.A1, U3.A2, U3.GND, Q10.EMITTER, Q11.EMITTER, Q12.EMITTER
  N4: Raspberry_Pi_1.GPIO17, R5.Pin_0
  N5: Raspberry_Pi_1.GPIO27, R6.Pin_0
  N6: Raspberry_Pi_1.GPIO22, R7.Pin_1
  N7: Raspberry_Pi_1.GPIO10, Onderdeel1.MOSI, ADC1.Din
  N8: Raspberry_Pi_1.GPIO9, Onderdeel1.MISO, ADC1.Dout
  N9: Raspberry_Pi_1.GPIO11, Onderdeel1.SCK, ADC1.CLK
  N10: Raspberry_Pi_1.GPIO5, R8.Pin_1
  N11: Raspberry_Pi_1.GPIO6, Matrix_keypad1.row1
  N12: Raspberry_Pi_1.GPIO13, Matrix_keypad1.row2
  N13: Raspberry_Pi_1.GPIO19, Matrix_keypad1.row3
  N14: Raspberry_Pi_1.GPIO26, Matrix_keypad1.row4
  N15: Raspberry_Pi_1.GPIO12, R27.Pin_0
  N16: Raspberry_Pi_1.GPIO7, ADC1.CS/SHDN
  N17: Raspberry_Pi_1.GPIO8, Onderdeel1.SDA
  N18: Raspberry_Pi_1.GPIO25, Onderdeel1.RST
  N19: Raspberry_Pi_1.GPIO24, LCD1.E
  N20: Raspberry_Pi_1.GPIO23, LCD1.RS
  5V: Raspberry_Pi_1.5V, LCD1.VDD, LCD1.LED+
  N21: LCD1.V0, R1.wiper
  N22: LCD1.DB0, U2.P0
  N23: LCD1.DB1, U2.P1
  N24: LCD1.DB2, U2.P2
  N25: LCD1.DB3, U2.P3
  N26: LCD1.DB4, U2.P4
  N27: LCD1.DB5, U2.P5
  N28: LCD1.DB6, U2.P6
  N29: LCD1.DB7, U2.P7
  N30: R3.Pin_0, U2.SDA, U3.SCL
  N31: Matrix_keypad1.col1, R5.Pin_1
  N32: Matrix_keypad1.col2, R6.Pin_1, Q12.BASE, R24.Pin_1
  N33: Matrix_keypad1.col3, R7.Pin_0
  N34: Matrix_keypad1.col4, R8.Pin_0
  GND_2: J1.PWR, LPD8806_RGB_LED_Strip1.GND, LPD8806_RGB_LED_Strip2.GND
  N35: LPD8806_RGB_LED_Strip1.DI, Q9.COLLECTOR
  N36: LPD8806_RGB_LED_Strip1.CI, Q8.COLLECTOR
  N37: LPD8806_RGB_LED_Strip1.+5V, Q7.COLLECTOR
  N38: ADC1.CH0, R29.Pin_1
  N39: ADC1.CH1, R30.Pin_1
  N40: ADC1.CH2, R11.pin_0, R20.Pin_1
  N41: ADC1.CH3, R14.pin_0, R19.Pin_1
  N42: ADC1.CH4, R13.pin_0, R18.Pin_1
  N43: ADC1.CH6, R10.pin_0, R16.Pin_1
  N44: ADC1.CH7, R9.pin_0, R15.Pin_1
  N45: R12.pin_0, R17.Pin_1
  N46: Q5.BASE, R27.Pin_1
  N47: Q6.BASE, R28.Pin_1
  N48: Q7.BASE, R21.Pin_1
  N49: Q8.BASE, R22.Pin_1
  N50: Q9.BASE, R23.Pin_1
  N51: U3.P2, R26.Pin_0
  N52: U3.P3, R25.Pin_0
  N53: U3.P4, R21.Pin_0
  N54: U3.P5, R22.Pin_0
  N55: U3.P6, R23.Pin_0
  N56: U3.P7, R24.Pin_0
  N57: Q10.COLLECTOR, LPD8806_RGB_LED_Strip2.DI
  N58: Q11.BASE, R26.Pin_1
  N59: Q11.COLLECTOR, LPD8806_RGB_LED_Strip2.CI

notes:
  +12V
  B
  R
  G
  12v GND
  Slot 1
  12v GND
  Slot 2
  3.3v GND
  Magneet
  sensor2
  Magneetsensor1
  3.3v GND
  VCC GND RXD TXD PRWDWN
  2D scanner

custom parts:
  KEYPAD 4x4: Matrix keypad 16 buttons, 4 rows x 4 columns
  RFID-RC522-v2: A simple China made RFID-RC522 Reader; do check the pin labels, as this is a MFRC522 based clone.
  LPD8806 RGB LED Strip: Digitally addressable RGB LED strip
